# Fritzing sketch carBlynk4Motor (saved by Fritzing 0.8.7b)

parts:
  M1 = Stepper Motor - Bipolar
  M2 = Stepper Motor - Bipolar
  M3 = Stepper Motor - Bipolar  # not connected
  M4 = Stepper Motor - Bipolar  # not connected
  U1 = ESP8266 NodeMCU LoLin base
  S1 = H-Bridge with L298N
  VCC1 = Battery block 9V

nets:
  N1: M1.B, S1.M2-02
  N2: M1.D, S1.M2-01
  N3: M2.A, S1.M1-02
  N4: M2.C, S1.M1-01
  N5: U1.D0-0, S1.ENA
  N6: U1.D1-0, S1.IN1
  N7: U1.D2-0, S1.IN2
  N8: U1.GND2-0, U1.GND3-2, S1.GND, VCC1.-
  N9: U1.D5-0, S1.ENB
  N10: U1.D6-0, S1.IN3
  N11: U1.D7-0, S1.IN4
  VIN: U1.VIN, U1.5V-3, S1.5V
  N12: S1.12V, VCC1.+

custom parts:
  ESP8266 NodeMCU LoLin base: ESP8266 based NodeMCU Base
  H-Bridge with L298N: h-bridge
  Battery block 9V: 9 Volt battery block with 200mil pcb footprint spacing
